// Logisim project 16bit_register_final.circ as structural Verilog: 1 circuit, main circuit main
module main (
  input  [1:0] s1_s0,
  input  E,
  input  I0,
  input  I1,
  input  I2,
  input  I3,
  input  I4,
  input  I5,
  input  I6,
  input  I7,
  input  I8,
  input  I9,
  input  I10,
  input  I11,
  input  I12,
  input  I13,
  input  I14,
  input  I15,
  output out_19,
  output out_20,
  output out_21,
  output out_22,
  output out_23,
  output out_24,
  output out_25,
  output out_26,
  output out_27,
  output out_28,
  output out_29,
  output out_30,
  output out_31,
  output out_32,
  output out_33,
  output out_34
);

  wire adder_1_cout, adder_1_out, adder_2_cout, adder_2_out, adder_3_cout, adder_3_out, adder_4_cout,
       adder_4_out, adder_5_cout, adder_5_out, adder_6_cout, adder_6_out, adder_7_cout, adder_7_out,
       adder_8_cout, adder_8_out, adder_9_cout, adder_9_out, adder_10_cout, adder_10_out, adder_11_cout,
       adder_11_out, adder_12_cout, adder_12_out, adder_13_cout, adder_13_out, adder_14_cout, adder_14_out,
       adder_15_cout, adder_15_out, adder_16_out, clock_1_out, multiplexer_1_out, multiplexer_2_out,
       multiplexer_3_out, multiplexer_4_out, multiplexer_5_out, multiplexer_6_out, multiplexer_7_out,
       multiplexer_8_out, multiplexer_9_out, multiplexer_10_out, multiplexer_11_out, multiplexer_12_out,
       multiplexer_13_out, multiplexer_14_out, multiplexer_15_out, multiplexer_16_out, subtractor_1_bout,
       subtractor_1_out, subtractor_2_bout, subtractor_2_out, subtractor_3_bout, subtractor_3_out,
       subtractor_4_bout, subtractor_4_out, subtractor_5_bout, subtractor_5_out, subtractor_6_bout,
       subtractor_6_out, subtractor_7_bout, subtractor_7_out, subtractor_8_bout, subtractor_8_out,
       subtractor_9_bout, subtractor_9_out, subtractor_10_bout, subtractor_10_out, subtractor_11_bout,
       subtractor_11_out, subtractor_12_bout, subtractor_12_out, subtractor_13_bout, subtractor_13_out,
       subtractor_14_bout, subtractor_14_out, subtractor_15_bout, subtractor_15_out, subtractor_16_out;

  Hex_Digit_Display hex_digit_display_1 (.value({I15, I14, I13, I12}));  // open: dp
  Hex_Digit_Display hex_digit_display_2 (.value({I11, I10, I9, I8}));  // open: dp
  Hex_Digit_Display hex_digit_display_3 (.value({I7, I6, I5, I4}));  // open: dp
  Hex_Digit_Display hex_digit_display_4 (.value({I3, I2, I1, I0}));  // open: dp
  Subtractor #(.width(1)) subtractor_1 (
    .a(out_19), .b(1'b1), .out(subtractor_1_out), .bout(subtractor_1_bout));  // open: bin
  Subtractor #(.width(1)) subtractor_2 (
    .a(out_20), .b(subtractor_1_bout), .out(subtractor_2_out), .bout(subtractor_2_bout));  // open: bin
  Subtractor #(.width(1)) subtractor_3 (
    .a(out_21), .b(subtractor_2_bout), .out(subtractor_3_out), .bout(subtractor_3_bout));  // open: bin
  Subtractor #(.width(1)) subtractor_4 (
    .a(out_22), .b(subtractor_3_bout), .out(subtractor_4_out), .bout(subtractor_4_bout));  // open: bin
  Subtractor #(.width(1)) subtractor_5 (
    .a(out_23), .b(subtractor_4_bout), .out(subtractor_5_out), .bout(subtractor_5_bout));  // open: bin
  Subtractor #(.width(1)) subtractor_6 (
    .a(out_24), .b(subtractor_5_bout), .out(subtractor_6_out), .bout(subtractor_6_bout));  // open: bin
  Subtractor #(.width(1)) subtractor_7 (
    .a(out_25), .b(subtractor_6_bout), .out(subtractor_7_out), .bout(subtractor_7_bout));  // open: bin
  Subtractor #(.width(1)) subtractor_8 (
    .a(out_26), .b(subtractor_7_bout), .out(subtractor_8_out), .bout(subtractor_8_bout));  // open: bin
  Subtractor #(.width(1)) subtractor_9 (
    .a(out_27), .b(subtractor_8_bout), .out(subtractor_9_out), .bout(subtractor_9_bout));  // open: bin
  Subtractor #(.width(1)) subtractor_10 (
    .a(out_28), .b(subtractor_9_bout), .out(subtractor_10_out), .bout(subtractor_10_bout));  // open: bin
  Subtractor #(.width(1)) subtractor_11 (
    .a(out_29), .b(subtractor_10_bout), .out(subtractor_11_out), .bout(subtractor_11_bout));  // open: bin
  Subtractor #(.width(1)) subtractor_12 (
    .a(out_30), .b(subtractor_11_bout), .out(subtractor_12_out), .bout(subtractor_12_bout));  // open: bin
  Subtractor #(.width(1)) subtractor_13 (
    .a(out_31), .b(subtractor_12_bout), .out(subtractor_13_out), .bout(subtractor_13_bout));  // open: bin
  Subtractor #(.width(1)) subtractor_14 (
    .a(out_32), .b(subtractor_13_bout), .out(subtractor_14_out), .bout(subtractor_14_bout));  // open: bin
  Subtractor #(.width(1)) subtractor_15 (
    .a(out_33), .b(subtractor_14_bout), .out(subtractor_15_out), .bout(subtractor_15_bout));  // open: bin
  Subtractor #(.width(1)) subtractor_16 (
    .a(out_34), .b(subtractor_15_bout), .out(subtractor_16_out));  // open: bin, bout
  Adder #(.width(1)) adder_1 (.a(out_19), .b(1'b1), .out(adder_1_out), .cout(adder_1_cout));  // open: cin
  Adder #(.width(1)) adder_2 (.a(out_20), .b(adder_1_cout), .out(adder_2_out), .cout(adder_2_cout));  // open: cin
  Adder #(.width(1)) adder_3 (.a(out_21), .b(adder_2_cout), .out(adder_3_out), .cout(adder_3_cout));  // open: cin
  Adder #(.width(1)) adder_4 (.a(out_22), .b(adder_3_cout), .out(adder_4_out), .cout(adder_4_cout));  // open: cin
  Adder #(.width(1)) adder_5 (.a(out_23), .b(adder_4_cout), .out(adder_5_out), .cout(adder_5_cout));  // open: cin
  Adder #(.width(1)) adder_6 (.a(out_24), .b(adder_5_cout), .out(adder_6_out), .cout(adder_6_cout));  // open: cin
  Adder #(.width(1)) adder_7 (.a(out_25), .b(adder_6_cout), .out(adder_7_out), .cout(adder_7_cout));  // open: cin
  Adder #(.width(1)) adder_8 (.a(out_26), .b(adder_7_cout), .out(adder_8_out), .cout(adder_8_cout));  // open: cin
  Adder #(.width(1)) adder_9 (.a(out_27), .b(adder_8_cout), .out(adder_9_out), .cout(adder_9_cout));  // open: cin
  Adder #(.width(1)) adder_10 (.a(out_28), .b(adder_9_cout), .out(adder_10_out), .cout(adder_10_cout));  // open: cin
  Adder #(.width(1)) adder_11 (.a(out_29), .b(adder_10_cout), .out(adder_11_out), .cout(adder_11_cout));  // open: cin
  Adder #(.width(1)) adder_12 (.a(out_30), .b(adder_11_cout), .out(adder_12_out), .cout(adder_12_cout));  // open: cin
  Adder #(.width(1)) adder_13 (.a(out_31), .b(adder_12_cout), .out(adder_13_out), .cout(adder_13_cout));  // open: cin
  Adder #(.width(1)) adder_14 (.a(out_32), .b(adder_13_cout), .out(adder_14_out), .cout(adder_14_cout));  // open: cin
  Adder #(.width(1)) adder_15 (.a(out_33), .b(adder_14_cout), .out(adder_15_out), .cout(adder_15_cout));  // open: cin
  Adder #(.width(1)) adder_16 (.a(out_34), .b(adder_15_cout), .out(adder_16_out));  // open: cin, cout
  Multiplexer #(.select(2)) multiplexer_1 (
    .in0(1'b0), .in1(I0), .in2(adder_1_out), .in3(subtractor_1_out), .out(multiplexer_1_out), .sel(s1_s0));  // open: en
  Multiplexer #(.select(2)) multiplexer_2 (
    .in0(1'b0), .in1(I1), .in2(adder_2_out), .in3(subtractor_2_out), .out(multiplexer_2_out), .sel(s1_s0));  // open: en
  Multiplexer #(.select(2)) multiplexer_3 (
    .in0(1'b0), .in1(I2), .in2(adder_3_out), .in3(subtractor_3_out), .out(multiplexer_3_out), .sel(s1_s0));  // open: en
  Multiplexer #(.select(2)) multiplexer_4 (
    .in0(1'b0), .in1(I3), .in2(adder_4_out), .in3(subtractor_4_out), .out(multiplexer_4_out), .sel(s1_s0));  // open: en
  Multiplexer #(.select(2)) multiplexer_5 (
    .in0(1'b0), .in1(I4), .in2(adder_5_out), .in3(subtractor_5_out), .out(multiplexer_5_out), .sel(s1_s0));  // open: en
  Multiplexer #(.select(2)) multiplexer_6 (
    .in0(1'b0), .in1(I5), .in2(adder_6_out), .in3(subtractor_6_out), .out(multiplexer_6_out), .sel(s1_s0));  // open: en
  Multiplexer #(.select(2)) multiplexer_7 (
    .in0(1'b0), .in1(I6), .in2(adder_7_out), .in3(subtractor_7_out), .out(multiplexer_7_out), .sel(s1_s0));  // open: en
  Multiplexer #(.select(2)) multiplexer_8 (
    .in0(1'b0), .in1(I7), .in2(adder_8_out), .in3(subtractor_8_out), .out(multiplexer_8_out), .sel(s1_s0));  // open: en
  Multiplexer #(.select(2)) multiplexer_9 (
    .in0(1'b0), .in1(I8), .in2(adder_9_out), .in3(subtractor_9_out), .out(multiplexer_9_out), .sel(s1_s0));  // open: en
  Multiplexer #(.select(2)) multiplexer_10 (
    .in0(1'b0), .in1(I9), .in2(adder_10_out), .in3(subtractor_10_out), .out(multiplexer_10_out), .sel(s1_s0));  // open: en
  Multiplexer #(.select(2)) multiplexer_11 (
    .in0(1'b0), .in1(I10), .in2(adder_11_out), .in3(subtractor_11_out), .out(multiplexer_11_out), .sel(s1_s0));  // open: en
  Multiplexer #(.select(2)) multiplexer_12 (
    .in0(1'b0), .in1(I11), .in2(adder_12_out), .in3(subtractor_12_out), .out(multiplexer_12_out), .sel(s1_s0));  // open: en
  Multiplexer #(.select(2)) multiplexer_13 (
    .in0(1'b0), .in1(I12), .in2(adder_13_out), .in3(subtractor_13_out), .out(multiplexer_13_out), .sel(s1_s0));  // open: en
  Multiplexer #(.select(2)) multiplexer_14 (
    .in0(1'b0), .in1(I13), .in2(adder_14_out), .in3(subtractor_14_out), .out(multiplexer_14_out), .sel(s1_s0));  // open: en
  Multiplexer #(.select(2)) multiplexer_15 (
    .in0(1'b0), .in1(I14), .in2(adder_15_out), .in3(subtractor_15_out), .out(multiplexer_15_out), .sel(s1_s0));  // open: en
  Multiplexer #(.select(2)) multiplexer_16 (
    .in0(1'b0), .in1(I15), .in2(adder_16_out), .in3(subtractor_16_out), .out(multiplexer_16_out), .sel(s1_s0));  // open: en
  Clock clock_1 (.out(clock_1_out));
  D_Flip_Flop d_ff_1 (.clk(clock_1_out), .D(multiplexer_1_out), .Q(out_19), .en(E));  // open: Qn, preset, reset
  D_Flip_Flop d_ff_2 (.clk(clock_1_out), .D(multiplexer_2_out), .Q(out_20), .en(E));  // open: Qn, preset, reset
  D_Flip_Flop d_ff_3 (.clk(clock_1_out), .D(multiplexer_3_out), .Q(out_21), .en(E));  // open: Qn, preset, reset
  D_Flip_Flop d_ff_4 (.clk(clock_1_out), .D(multiplexer_4_out), .Q(out_22), .en(E));  // open: Qn, preset, reset
  D_Flip_Flop d_ff_5 (.clk(clock_1_out), .D(multiplexer_5_out), .Q(out_23), .en(E));  // open: Qn, preset, reset
  D_Flip_Flop d_ff_6 (.clk(clock_1_out), .D(multiplexer_6_out), .Q(out_24), .en(E));  // open: Qn, preset, reset
  D_Flip_Flop d_ff_7 (.clk(clock_1_out), .D(multiplexer_7_out), .Q(out_25), .en(E));  // open: Qn, preset, reset
  D_Flip_Flop d_ff_8 (.clk(clock_1_out), .D(multiplexer_8_out), .Q(out_26), .en(E));  // open: Qn, preset, reset
  D_Flip_Flop d_ff_9 (.clk(clock_1_out), .D(multiplexer_9_out), .Q(out_27), .en(E));  // open: Qn, preset, reset
  D_Flip_Flop d_ff_10 (.clk(clock_1_out), .D(multiplexer_10_out), .Q(out_28), .en(E));  // open: Qn, preset, reset
  D_Flip_Flop d_ff_11 (.clk(clock_1_out), .D(multiplexer_11_out), .Q(out_29), .en(E));  // open: Qn, preset, reset
  D_Flip_Flop d_ff_12 (.clk(clock_1_out), .D(multiplexer_12_out), .Q(out_30), .en(E));  // open: Qn, preset, reset
  D_Flip_Flop d_ff_13 (.clk(clock_1_out), .D(multiplexer_13_out), .Q(out_31), .en(E));  // open: Qn, preset, reset
  D_Flip_Flop d_ff_14 (.clk(clock_1_out), .D(multiplexer_14_out), .Q(out_32), .en(E));  // open: Qn, preset, reset
  D_Flip_Flop d_ff_15 (.clk(clock_1_out), .D(multiplexer_15_out), .Q(out_33), .en(E));  // open: Qn, preset, reset
  D_Flip_Flop d_ff_16 (.clk(clock_1_out), .D(multiplexer_16_out), .Q(out_34), .en(E));  // open: Qn, preset, reset
  Hex_Digit_Display hex_digit_display_5 (.value({out_34, out_33, out_32, out_31}));  // open: dp
  Hex_Digit_Display hex_digit_display_6 (.value({out_30, out_29, out_28, out_27}));  // open: dp
  Hex_Digit_Display hex_digit_display_7 (.value({out_26, out_25, out_24, out_23}));  // open: dp
  Hex_Digit_Display hex_digit_display_8 (.value({out_22, out_21, out_20, out_19}));  // open: dp
endmodule
