// Logisim project 8bit_register_final.circ as structural Verilog: 1 circuit, main circuit main
module main (
  input  [1:0] s1_s0,
  input  E,
  input  I0,
  input  I1,
  input  I2,
  input  I3,
  input  I4,
  input  I5,
  input  I6,
  input  I7,
  output out_11,
  output out_12,
  output out_13,
  output out_14,
  output out_15,
  output out_16,
  output out_17,
  output out_18
);

  wire adder_1_cout, adder_1_out, adder_2_cout, adder_2_out, adder_3_cout, adder_3_out, adder_4_cout,
       adder_4_out, adder_5_cout, adder_5_out, adder_6_cout, adder_6_out, adder_7_cout, adder_7_out,
       adder_8_out, clock_1_out, multiplexer_1_out, multiplexer_2_out, multiplexer_3_out, multiplexer_4_out,
       multiplexer_5_out, multiplexer_6_out, multiplexer_7_out, multiplexer_8_out, subtractor_1_bout,
       subtractor_1_out, subtractor_2_bout, subtractor_2_out, subtractor_3_bout, subtractor_3_out,
       subtractor_4_bout, subtractor_4_out, subtractor_5_bout, subtractor_5_out, subtractor_6_bout,
       subtractor_6_out, subtractor_7_bout, subtractor_7_out, subtractor_8_out;

  Hex_Digit_Display hex_digit_display_1 (.value({I7, I6, I5, I4}));  // open: dp
  Hex_Digit_Display hex_digit_display_2 (.value({I3, I2, I1, I0}));  // open: dp
  Subtractor #(.width(1)) subtractor_1 (
    .a(out_11), .b(1'b1), .out(subtractor_1_out), .bout(subtractor_1_bout));  // open: bin
  Subtractor #(.width(1)) subtractor_2 (
    .a(out_12), .b(subtractor_1_bout), .out(subtractor_2_out), .bout(subtractor_2_bout));  // open: bin
  Subtractor #(.width(1)) subtractor_3 (
    .a(out_13), .b(subtractor_2_bout), .out(subtractor_3_out), .bout(subtractor_3_bout));  // open: bin
  Subtractor #(.width(1)) subtractor_4 (
    .a(out_14), .b(subtractor_3_bout), .out(subtractor_4_out), .bout(subtractor_4_bout));  // open: bin
  Subtractor #(.width(1)) subtractor_5 (
    .a(out_15), .b(subtractor_4_bout), .out(subtractor_5_out), .bout(subtractor_5_bout));  // open: bin
  Subtractor #(.width(1)) subtractor_6 (
    .a(out_16), .b(subtractor_5_bout), .out(subtractor_6_out), .bout(subtractor_6_bout));  // open: bin
  Subtractor #(.width(1)) subtractor_7 (
    .a(out_17), .b(subtractor_6_bout), .out(subtractor_7_out), .bout(subtractor_7_bout));  // open: bin
  Subtractor #(.width(1)) subtractor_8 (.a(out_18), .b(subtractor_7_bout), .out(subtractor_8_out));  // open: bin, bout
  Adder #(.width(1)) adder_1 (.a(out_11), .b(1'b1), .out(adder_1_out), .cout(adder_1_cout));  // open: cin
  Adder #(.width(1)) adder_2 (.a(out_12), .b(adder_1_cout), .out(adder_2_out), .cout(adder_2_cout));  // open: cin
  Adder #(.width(1)) adder_3 (.a(out_13), .b(adder_2_cout), .out(adder_3_out), .cout(adder_3_cout));  // open: cin
  Adder #(.width(1)) adder_4 (.a(out_14), .b(adder_3_cout), .out(adder_4_out), .cout(adder_4_cout));  // open: cin
  Adder #(.width(1)) adder_5 (.a(out_15), .b(adder_4_cout), .out(adder_5_out), .cout(adder_5_cout));  // open: cin
  Adder #(.width(1)) adder_6 (.a(out_16), .b(adder_5_cout), .out(adder_6_out), .cout(adder_6_cout));  // open: cin
  Adder #(.width(1)) adder_7 (.a(out_17), .b(adder_6_cout), .out(adder_7_out), .cout(adder_7_cout));  // open: cin
  Adder #(.width(1)) adder_8 (.a(out_18), .b(adder_7_cout), .out(adder_8_out));  // open: cin, cout
  Multiplexer #(.select(2)) multiplexer_1 (
    .in0(1'b0), .in1(I0), .in2(adder_1_out), .in3(subtractor_1_out), .out(multiplexer_1_out), .sel(s1_s0));  // open: en
  Multiplexer #(.select(2)) multiplexer_2 (
    .in0(1'b0), .in1(I1), .in2(adder_2_out), .in3(subtractor_2_out), .out(multiplexer_2_out), .sel(s1_s0));  // open: en
  Multiplexer #(.select(2)) multiplexer_3 (
    .in0(1'b0), .in1(I2), .in2(adder_3_out), .in3(subtractor_3_out), .out(multiplexer_3_out), .sel(s1_s0));  // open: en
  Multiplexer #(.select(2)) multiplexer_4 (
    .in0(1'b0), .in1(I3), .in2(adder_4_out), .in3(subtractor_4_out), .out(multiplexer_4_out), .sel(s1_s0));  // open: en
  Multiplexer #(.select(2)) multiplexer_5 (
    .in0(1'b0), .in1(I4), .in2(adder_5_out), .in3(subtractor_5_out), .out(multiplexer_5_out), .sel(s1_s0));  // open: en
  Multiplexer #(.select(2)) multiplexer_6 (
    .in0(1'b0), .in1(I5), .in2(adder_6_out), .in3(subtractor_6_out), .out(multiplexer_6_out), .sel(s1_s0));  // open: en
  Multiplexer #(.select(2)) multiplexer_7 (
    .in0(1'b0), .in1(I6), .in2(adder_7_out), .in3(subtractor_7_out), .out(multiplexer_7_out), .sel(s1_s0));  // open: en
  Multiplexer #(.select(2)) multiplexer_8 (
    .in0(1'b0), .in1(I7), .in2(adder_8_out), .in3(subtractor_8_out), .out(multiplexer_8_out), .sel(s1_s0));  // open: en
  Clock clock_1 (.out(clock_1_out));
  D_Flip_Flop d_ff_1 (.clk(clock_1_out), .D(multiplexer_1_out), .Q(out_11), .en(E));  // open: Qn, preset, reset
  D_Flip_Flop d_ff_2 (.clk(clock_1_out), .D(multiplexer_2_out), .Q(out_12), .en(E));  // open: Qn, preset, reset
  D_Flip_Flop d_ff_3 (.clk(clock_1_out), .D(multiplexer_3_out), .Q(out_13), .en(E));  // open: Qn, preset, reset
  D_Flip_Flop d_ff_4 (.clk(clock_1_out), .D(multiplexer_4_out), .Q(out_14), .en(E));  // open: Qn, preset, reset
  D_Flip_Flop d_ff_5 (.clk(clock_1_out), .D(multiplexer_5_out), .Q(out_15), .en(E));  // open: Qn, preset, reset
  D_Flip_Flop d_ff_6 (.clk(clock_1_out), .D(multiplexer_6_out), .Q(out_16), .en(E));  // open: Qn, preset, reset
  D_Flip_Flop d_ff_7 (.clk(clock_1_out), .D(multiplexer_7_out), .Q(out_17), .en(E));  // open: Qn, preset, reset
  D_Flip_Flop d_ff_8 (.clk(clock_1_out), .D(multiplexer_8_out), .Q(out_18), .en(E));  // open: Qn, preset, reset
  Hex_Digit_Display hex_digit_display_3 (.value({out_18, out_17, out_16, out_15}));  // open: dp
  Hex_Digit_Display hex_digit_display_4 (.value({out_14, out_13, out_12, out_11}));  // open: dp
endmodule
