// Logisim project Arithmetic_Unit.circ as structural Verilog: 1 circuit, main circuit main
module main (
  input  s1,
  input  s0,
  input  CARRY,
  input  A0,
  input  B0,
  input  A1,
  input  B1,
  input  A2,
  input  B2,
  input  A3,
  input  B3,
  input  A4,
  input  B4,
  input  A5,
  input  B5,
  input  A6,
  input  B6,
  input  A7,
  input  B7,
  output O0,
  output O1,
  output O2,
  output O3,
  output O4,
  output O5,
  output O6,
  output O7,
  output C_OUT_FLAG
);

  wire adder_1_cout, adder_2_cout, adder_3_cout, adder_4_cout, adder_5_cout, adder_6_cout, adder_7_cout,
       multiplexer_1_out, multiplexer_2_out, xor_1_out, xor_2_out, xor_3_out, xor_4_out, xor_5_out,
       xor_6_out, xor_7_out, xor_8_out;

  xor xor_1 (xor_1_out, s1, B0);
  xor xor_2 (xor_2_out, s1, B1);
  xor xor_3 (xor_3_out, s1, B2);
  xor xor_4 (xor_4_out, s1, B3);
  xor xor_5 (xor_5_out, s1, B4);
  xor xor_6 (xor_6_out, s1, B5);
  xor xor_7 (xor_7_out, s1, B6);
  xor xor_8 (xor_8_out, s1, B7);
  Multiplexer #(.enable("false")) multiplexer_1 (.in0(1'b0), .in1(1'b1), .out(multiplexer_1_out), .sel(s1));
  Adder #(.width(1)) adder_1 (.a(A0), .b(xor_1_out), .out(O0), .cin(multiplexer_2_out), .cout(adder_1_cout));
  Adder #(.width(1)) adder_2 (.a(A1), .b(xor_2_out), .out(O1), .cin(adder_1_cout), .cout(adder_2_cout));
  Adder #(.width(1)) adder_3 (.a(A2), .b(xor_3_out), .out(O2), .cin(adder_2_cout), .cout(adder_3_cout));
  Adder #(.width(1)) adder_4 (.a(A3), .b(xor_4_out), .out(O3), .cin(adder_3_cout), .cout(adder_4_cout));
  Adder #(.width(1)) adder_5 (.a(A4), .b(xor_5_out), .out(O4), .cin(adder_4_cout), .cout(adder_5_cout));
  Adder #(.width(1)) adder_6 (.a(A5), .b(xor_6_out), .out(O5), .cin(adder_5_cout), .cout(adder_6_cout));
  Adder #(.width(1)) adder_7 (.a(A6), .b(xor_7_out), .out(O6), .cin(adder_6_cout), .cout(adder_7_cout));
  Adder #(.width(1)) adder_8 (.a(A7), .b(xor_8_out), .out(O7), .cin(adder_7_cout), .cout(C_OUT_FLAG));
  Multiplexer #(.enable("false")) multiplexer_2 (
    .in0(multiplexer_1_out), .in1(CARRY), .out(multiplexer_2_out), .sel(s0));
endmodule
