// Logisim project Logic_Unit.circ as structural Verilog: 1 circuit, main circuit main
module main (
  input  A0,
  input  B0,
  input  A1,
  input  B1,
  input  A2,
  input  B2,
  input  A3,
  input  B3,
  input  A4,
  input  B4,
  input  A5,
  input  B5,
  input  A6,
  input  B6,
  input  A7,
  input  B7,
  output A0_2,
  output B0_2,
  output NOTA0,
  output NOTB0,
  output AND0,
  output OR0,
  output XOR0,
  output A1_2,
  output B1_2,
  output NOTA1,
  output NOTB1,
  output AND1,
  output OR1,
  output XOR1,
  output A2_2,
  output B2_2,
  output NOTA2,
  output NOTB2,
  output AND2,
  output OR2,
  output XOR2,
  output A3_2,
  output B3_2,
  output NOTA3,
  output NOTB3,
  output AND3,
  output OR3,
  output XOR3,
  output A4_2,
  output B4_2,
  output NOTA4,
  output NOTB4,
  output AND4,
  output OR4,
  output XOR4,
  output A5_2,
  output B5_2,
  output NOTA5,
  output NOTB5,
  output AND5,
  output OR5,
  output XOR5,
  output A6_2,
  output B6_2,
  output NOTA6,
  output NOTB6,
  output AND6,
  output OR6,
  output XOR6,
  output A7_2,
  output B7_2,
  output NOTA7,
  output NOTB7,
  output AND7,
  output OR7,
  output XOR7
);

  not not_1 (NOTA0, A0);
  not not_2 (NOTB0, B0);
  and and_1 (AND0, A0, B0);
  or or_1 (OR0, A0, B0);
  xor xor_1 (XOR0, A0, B0);
  not not_3 (NOTA1, A1);
  not not_4 (NOTB1, B1);
  and and_2 (AND1, A1, B1);
  or or_2 (OR1, A1, B1);
  xor xor_2 (XOR1, A1, B1);
  not not_5 (NOTA2, A2);
  not not_6 (NOTB2, B2);
  and and_3 (AND2, A2, B2);
  or or_3 (OR2, A2, B2);
  xor xor_3 (XOR2, A2, B2);
  not not_7 (NOTA3, A3);
  not not_8 (NOTB3, B3);
  and and_4 (AND3, A3, B3);
  or or_4 (OR3, A3, B3);
  xor xor_4 (XOR3, A3, B3);
  not not_9 (NOTA4, A4);
  not not_10 (NOTB4, B4);
  and and_5 (AND4, A4, B4);
  or or_5 (OR4, A4, B4);
  xor xor_5 (XOR4, A4, B4);
  not not_11 (NOTA5, A5);
  not not_12 (NOTB5, B5);
  and and_6 (AND5, A5, B5);
  or or_6 (OR5, A5, B5);
  xor xor_6 (XOR5, A5, B5);
  not not_13 (NOTA6, A6);
  not not_14 (NOTB6, B6);
  and and_7 (AND6, A6, B6);
  or or_7 (OR6, A6, B6);
  xor xor_7 (XOR6, A6, B6);
  not not_15 (NOTA7, A7);
  not not_16 (NOTB7, B7);
  and and_8 (AND7, A7, B7);
  or or_8 (OR7, A7, B7);
  xor xor_8 (XOR7, A7, B7);

  assign A0_2 = A0;
  assign A1_2 = A1;
  assign A2_2 = A2;
  assign A3_2 = A3;
  assign A4_2 = A4;
  assign A5_2 = A5;
  assign A6_2 = A6;
  assign A7_2 = A7;
  assign B0_2 = B0;
  assign B1_2 = B1;
  assign B2_2 = B2;
  assign B3_2 = B3;
  assign B4_2 = B4;
  assign B5_2 = B5;
  assign B6_2 = B6;
  assign B7_2 = B7;
endmodule
