// Logisim project Part1.circ as structural Verilog: 1 circuit, main circuit main
module main (
  input  [3:0] FunSel,
  input  A0,
  input  A1,
  input  A2,
  input  A3,
  input  A4,
  input  A5,
  input  A6,
  input  A7,
  input  B0,
  input  B1,
  input  B2,
  input  B3,
  input  B4,
  input  B5,
  input  B6,
  input  B7,
  output [3:0] ZCNO,
  output OutALU0,
  output OutALU1,
  output OutALU2,
  output OutALU3,
  output OutALU4,
  output OutALU5,
  output OutALU6,
  output OutALU7
);

  wire main_1_c_out_flag, main_1_o0, main_1_o1, main_1_o2, main_1_o3, main_1_o4, main_1_o5, main_1_o6,
       main_1_o7, main_2_a0_2, main_2_a1_2, main_2_a2_2, main_2_a3_2, main_2_a4_2, main_2_a5_2, main_2_a6_2,
       main_2_a7_2, main_2_and0, main_2_and1, main_2_and2, main_2_and3, main_2_and4, main_2_and5,
       main_2_and6, main_2_and7, main_2_b0_2, main_2_b1_2, main_2_b2_2, main_2_b3_2, main_2_b4_2,
       main_2_b5_2, main_2_b6_2, main_2_b7_2, main_2_nota0, main_2_nota1, main_2_nota2, main_2_nota3,
       main_2_nota4, main_2_nota5, main_2_nota6, main_2_nota7, main_2_notb0, main_2_notb1, main_2_notb2,
       main_2_notb3, main_2_notb4, main_2_notb5, main_2_notb6, main_2_notb7, main_2_or0, main_2_or1,
       main_2_or2, main_2_or3, main_2_or4, main_2_or5, main_2_or6, main_2_or7, main_2_xor0, main_2_xor1,
       main_2_xor2, main_2_xor3, main_2_xor4, main_2_xor5, main_2_xor6, main_2_xor7, main_3_carry_out,
       main_3_o0, main_3_o1, main_3_o2, main_3_o3, main_3_o4, main_3_o5, main_3_o6, main_3_o7;
  wire [3:0] adder_2_out, multiplexer_1_out, multiplexer_2_out, multiplexer_3_out, multiplexer_4_out,
       multiplexer_13_out, multiplexer_14_out;
  wire [7:0] adder_1_out, adder_3_out, not_1_out, not_2_out, not_3_out;
  wire [7:4] adder_2_out_2;

  assign not_1_out = ~{A7, A6, A5, A4, A3, A2, A1, A0};  // NOT_Gate not_1, 8 bits wide
  Hex_Digit_Display hex_digit_display_1 (.value({3'b000, A7}));  // open: dp
  Hex_Digit_Display hex_digit_display_2 (.value({3'b000, B7}));  // open: dp
  Adder adder_1 (.a(not_1_out), .b(8'h1), .out(adder_1_out));  // open: cin, cout
  Hex_Digit_Display hex_digit_display_3 (.value(multiplexer_2_out));  // open: dp
  Hex_Digit_Display hex_digit_display_4 (.value(multiplexer_4_out));  // open: dp
  assign not_2_out = ~{B7, B6, B5, B4, B3, B2, B1, B0};  // NOT_Gate not_2, 8 bits wide
  Hex_Digit_Display hex_digit_display_5 (.value(multiplexer_1_out));  // open: dp
  Hex_Digit_Display hex_digit_display_6 (.value(multiplexer_3_out));  // open: dp
  Adder adder_2 (.a(not_2_out), .b(8'h1), .out({adder_2_out_2, adder_2_out}));  // open: cin, cout
  Multiplexer #(.width(4), .enable("false")) multiplexer_1 (
    .in0({A3, A2, A1, A0}), .in1(adder_1_out[3:0]), .out(multiplexer_1_out), .sel(A7));
  Multiplexer #(.width(4), .enable("false")) multiplexer_2 (
    .in0({A7, A6, A5, A4}), .in1(adder_1_out[7:4]), .out(multiplexer_2_out), .sel(A7));
  Multiplexer #(.width(4), .enable("false")) multiplexer_3 (
    .in0({B3, B2, B1, B0}), .in1(adder_2_out), .out(multiplexer_3_out), .sel(B7));
  Multiplexer #(.width(4), .enable("false")) multiplexer_4 (
    .in0({B7, B6, B5, B4}), .in1(adder_2_out_2), .out(multiplexer_4_out), .sel(B7));
  Arithmetic_Unit_main main_1 (
    .s1(FunSel[1]), .s0(FunSel[0]), .CARRY(ZCNO[2]), .A0(A0), .B0(B0), .A1(A1), .B1(B1), .A2(A2), .B2(B2),
    .A3(A3), .B3(B3), .A4(A4), .B4(B4), .A5(A5), .B5(B5), .A6(A6), .B6(B6), .A7(A7), .B7(B7), .O0(main_1_o0),
    .O1(main_1_o1), .O2(main_1_o2), .O3(main_1_o3), .O4(main_1_o4), .O5(main_1_o5), .O6(main_1_o6),
    .O7(main_1_o7), .C_OUT_FLAG(main_1_c_out_flag));
  Logic_Unit_main main_2 (
    .A0(A0), .B0(B0), .A1(A1), .B1(B1), .A2(A2), .B2(B2), .A3(A3), .B3(B3), .A4(A4), .B4(B4), .A5(A5),
    .B5(B5), .A6(A6), .B6(B6), .A7(A7), .B7(B7), .A0_2(main_2_a0_2), .B0_2(main_2_b0_2),
    .NOTA0(main_2_nota0), .NOTB0(main_2_notb0), .AND0(main_2_and0), .OR0(main_2_or0), .XOR0(main_2_xor0),
    .A1_2(main_2_a1_2), .B1_2(main_2_b1_2), .NOTA1(main_2_nota1), .NOTB1(main_2_notb1), .AND1(main_2_and1),
    .OR1(main_2_or1), .XOR1(main_2_xor1), .A2_2(main_2_a2_2), .B2_2(main_2_b2_2), .NOTA2(main_2_nota2),
    .NOTB2(main_2_notb2), .AND2(main_2_and2), .OR2(main_2_or2), .XOR2(main_2_xor2), .A3_2(main_2_a3_2),
    .B3_2(main_2_b3_2), .NOTA3(main_2_nota3), .NOTB3(main_2_notb3), .AND3(main_2_and3), .OR3(main_2_or3),
    .XOR3(main_2_xor3), .A4_2(main_2_a4_2), .B4_2(main_2_b4_2), .NOTA4(main_2_nota4), .NOTB4(main_2_notb4),
    .AND4(main_2_and4), .OR4(main_2_or4), .XOR4(main_2_xor4), .A5_2(main_2_a5_2), .B5_2(main_2_b5_2),
    .NOTA5(main_2_nota5), .NOTB5(main_2_notb5), .AND5(main_2_and5), .OR5(main_2_or5), .XOR5(main_2_xor5),
    .A6_2(main_2_a6_2), .B6_2(main_2_b6_2), .NOTA6(main_2_nota6), .NOTB6(main_2_notb6), .AND6(main_2_and6),
    .OR6(main_2_or6), .XOR6(main_2_xor6), .A7_2(main_2_a7_2), .B7_2(main_2_b7_2), .NOTA7(main_2_nota7),
    .NOTB7(main_2_notb7), .AND7(main_2_and7), .OR7(main_2_or7), .XOR7(main_2_xor7));
  Shifting_Unit_main main_3 (
    .s2(FunSel[2]), .s1(FunSel[1]), .s0(FunSel[0]), .CARRY_IN(ZCNO[2]), .A0(A0), .A1(A1), .A2(A2), .A3(A3),
    .A4(A4), .A5(A5), .A6(A6), .A7(A7), .O0(main_3_o0), .O1(main_3_o1), .O2(main_3_o2), .O3(main_3_o3),
    .O4(main_3_o4), .O5(main_3_o5), .O6(main_3_o6), .O7(main_3_o7), .CARRY_OUT(main_3_carry_out));
  assign not_3_out = ~{OutALU7, OutALU6, OutALU5, OutALU4, OutALU3, OutALU2, OutALU1, OutALU0};  // NOT_Gate not_3, 8 bits wide
  Adder adder_3 (.a(not_3_out), .b(8'h1), .out(adder_3_out));  // open: cin, cout
  Multiplexer #(.select(4), .enable("false")) multiplexer_5 (
    .in0(main_2_a0_2), .in1(main_2_b0_2), .in2(main_2_nota0), .in3(main_2_notb0), .in4(main_1_o0),
    .in5(main_1_o0), .in6(main_1_o0), .in7(main_2_and0), .in8(main_2_or0), .in9(main_2_xor0),
    .in10(main_3_o0), .in11(main_3_o0), .in12(main_3_o0), .in13(main_3_o0), .in14(main_3_o0),
    .in15(main_3_o0), .out(OutALU0), .sel(FunSel));
  Multiplexer #(.select(4), .enable("false")) multiplexer_6 (
    .in0(main_2_a1_2), .in1(main_2_b1_2), .in2(main_2_nota1), .in3(main_2_notb1), .in4(main_1_o1),
    .in5(main_1_o1), .in6(main_1_o1), .in7(main_2_and1), .in8(main_2_or1), .in9(main_2_xor1),
    .in10(main_3_o1), .in11(main_3_o1), .in12(main_3_o1), .in13(main_3_o1), .in14(main_3_o1),
    .in15(main_3_o1), .out(OutALU1), .sel(FunSel));
  Multiplexer #(.select(4), .enable("false")) multiplexer_7 (
    .in0(main_2_a2_2), .in1(main_2_b2_2), .in2(main_2_nota2), .in3(main_2_notb2), .in4(main_1_o2),
    .in5(main_1_o2), .in6(main_1_o2), .in7(main_2_and2), .in8(main_2_or2), .in9(main_2_xor2),
    .in10(main_3_o2), .in11(main_3_o2), .in12(main_3_o2), .in13(main_3_o2), .in14(main_3_o2),
    .in15(main_3_o2), .out(OutALU2), .sel(FunSel));
  Multiplexer #(.select(4), .enable("false")) multiplexer_8 (
    .in0(main_2_a3_2), .in1(main_2_b3_2), .in2(main_2_nota3), .in3(main_2_notb3), .in4(main_1_o3),
    .in5(main_1_o3), .in6(main_1_o3), .in7(main_2_and3), .in8(main_2_or3), .in9(main_2_xor3),
    .in10(main_3_o3), .in11(main_3_o3), .in12(main_3_o3), .in13(main_3_o3), .in14(main_3_o3),
    .in15(main_3_o3), .out(OutALU3), .sel(FunSel));
  Multiplexer #(.select(4), .enable("false")) multiplexer_9 (
    .in0(main_2_a4_2), .in1(main_2_b4_2), .in2(main_2_nota4), .in3(main_2_notb4), .in4(main_1_o4),
    .in5(main_1_o4), .in6(main_1_o4), .in7(main_2_and4), .in8(main_2_or4), .in9(main_2_xor4),
    .in10(main_3_o4), .in11(main_3_o4), .in12(main_3_o4), .in13(main_3_o4), .in14(main_3_o4),
    .in15(main_3_o4), .out(OutALU4), .sel(FunSel));
  Multiplexer #(.select(4), .enable("false")) multiplexer_10 (
    .in0(main_2_a5_2), .in1(main_2_b5_2), .in2(main_2_nota5), .in3(main_2_notb5), .in4(main_1_o5),
    .in5(main_1_o5), .in6(main_1_o5), .in7(main_2_and5), .in8(main_2_or5), .in9(main_2_xor5),
    .in10(main_3_o5), .in11(main_3_o5), .in12(main_3_o5), .in13(main_3_o5), .in14(main_3_o5),
    .in15(main_3_o5), .out(OutALU5), .sel(FunSel));
  Multiplexer #(.select(4), .enable("false")) multiplexer_11 (
    .in0(main_2_a6_2), .in1(main_2_b6_2), .in2(main_2_nota6), .in3(main_2_notb6), .in4(main_1_o6),
    .in5(main_1_o6), .in6(main_1_o6), .in7(main_2_and6), .in8(main_2_or6), .in9(main_2_xor6),
    .in10(main_3_o6), .in11(main_3_o6), .in12(main_3_o6), .in13(main_3_o6), .in14(main_3_o6),
    .in15(main_3_o6), .out(OutALU6), .sel(FunSel));
  Multiplexer #(.select(4), .enable("false")) multiplexer_12 (
    .in0(main_2_a7_2), .in1(main_2_b7_2), .in2(main_2_nota7), .in3(main_2_notb7), .in4(main_1_o7),
    .in5(main_1_o7), .in6(main_1_o7), .in7(main_2_and7), .in8(main_2_or7), .in9(main_2_xor7),
    .in10(main_3_o7), .in11(main_3_o7), .in12(main_3_o7), .in13(main_3_o7), .in14(main_3_o7),
    .in15(main_3_o7), .out(OutALU7), .sel(FunSel));
  Multiplexer #(.width(4), .enable("false")) multiplexer_13 (
    .in0({OutALU3, OutALU2, OutALU1, OutALU0}), .in1(adder_3_out[3:0]), .out(multiplexer_13_out),
    .sel(OutALU7));
  Multiplexer #(.width(4), .enable("false")) multiplexer_14 (
    .in0({OutALU7, OutALU6, OutALU5, OutALU4}), .in1(adder_3_out[7:4]), .out(multiplexer_14_out),
    .sel(OutALU7));
  Hex_Digit_Display hex_digit_display_7 (.value({3'b000, OutALU7}));  // open: dp
  Hex_Digit_Display hex_digit_display_8 (.value(multiplexer_14_out));  // open: dp
  Hex_Digit_Display hex_digit_display_9 (.value(multiplexer_13_out));  // open: dp
  ZCNO_Register_main main_4 (
    .FunSel(FunSel), .OutALU0(OutALU0), .OutALU1(OutALU1), .OutALU2(OutALU2), .OutALU3(OutALU3),
    .OutALU4(OutALU4), .OutALU5(OutALU5), .OutALU6(OutALU6), .OutALU7(OutALU7),
    .C_arithmetic(main_1_c_out_flag), .C_shifting(main_3_carry_out), .A6(A6), .A7(A7), .B7(B7),
    .ZERO(ZCNO[3]), .CARRY(ZCNO[2]), .NEGATIVE(ZCNO[1]), .OVERFLOW(ZCNO[0]));

  // Notes on the sheet:
  //   Sign of A
  //   Sign of B
  //   Logic Unit
  //   Shifting Unit
  //   Arithmetic Unit
  //   Sign of OutALU
  //   ZCNO Register
endmodule
