// Logisim project Part2_corrected.circ as structural Verilog: 1 circuit, main circuit main
module main (
  input  [3:0] FunSel,
  input  MuxCSel,
  input  [3:0] RegSel,
  input  [1:0] FunSel_2,
  input  [1:0] OutBSel,
  input  [1:0] OutASel,
  input  CLR,
  input  [1:0] MuxASel,
  input  Str,
  input  Sel,
  input  [2:0] RegSel_2,
  input  LD,
  input  [1:0] FunSel_3,
  input  [1:0] OutDSel,
  input  [1:0] OutCSel,
  input  E,
  input  L_prime_H,
  input  [1:0] FunSel_4,
  input  [1:0] MuxBSel,
  output [7:0] OutB,
  output [7:0] OutA,
  output [7:0] MUX_C_Out,
  output [3:0] ZCNO,
  output [7:0] OutALU,
  output [7:0] D__load,
  output [7:0] MuxA_Out,
  output [7:0] OutC,
  output [7:0] IR_0_7,
  output [7:0] OutD,
  output [7:0] IR_8_15,
  output [7:0] MUX_B_Out
);

  wire CLK_out;

  Part2a_final_main main_1 (
    .OutASel(OutASel), .OutBSel(OutBSel), .FunSel(FunSel_2), .RegSel(RegSel), .I0(MuxA_Out[0]),
    .I1(MuxA_Out[1]), .I2(MuxA_Out[2]), .I3(MuxA_Out[3]), .I4(MuxA_Out[4]), .I5(MuxA_Out[5]),
    .I6(MuxA_Out[6]), .I7(MuxA_Out[7]), .OutA0(OutA[0]), .OutB0(OutB[0]), .OutA1(OutA[1]), .OutB1(OutB[1]),
    .OutA2(OutA[2]), .OutB2(OutB[2]), .OutA3(OutA[3]), .OutB3(OutB[3]), .OutA4(OutA[4]), .OutB4(OutB[4]),
    .OutA5(OutA[5]), .OutB5(OutB[5]), .OutA6(OutA[6]), .OutB6(OutB[6]), .OutA7(OutA[7]), .OutB7(OutB[7]));
  Multiplexer #(.select(2), .width(8), .enable("false")) multiplexer_1 (
    .in0(IR_0_7), .in1(D__load), .in2(OutC), .in3(OutALU), .out(MuxA_Out), .sel(MuxASel));
  Part2c_final_FunSel_main main_2 (
    .FunSel(FunSel_4), .L_prime_H(L_prime_H), .E(E), .I0(D__load[0]), .I1(D__load[1]), .I2(D__load[2]),
    .I3(D__load[3]), .I4(D__load[4]), .I5(D__load[5]), .I6(D__load[6]), .I7(D__load[7]), .O0(IR_0_7[0]),
    .O1(IR_0_7[1]), .O2(IR_0_7[2]), .O3(IR_0_7[3]), .O4(IR_0_7[4]), .O5(IR_0_7[5]), .O6(IR_0_7[6]),
    .O7(IR_0_7[7]), .O8(IR_8_15[0]), .O9(IR_8_15[1]), .O10(IR_8_15[2]), .O11(IR_8_15[3]), .O12(IR_8_15[4]),
    .O13(IR_8_15[5]), .O14(IR_8_15[6]), .O15(IR_8_15[7]));
  Multiplexer #(.width(8), .enable("false")) multiplexer_2 (.in0(MuxA_Out), .in1(OutA), .out(MUX_C_Out), .sel(MuxCSel));
  Multiplexer #(.select(2), .width(8), .enable("false")) multiplexer_3 (
    .in0({8{1'b0}}), .in1(IR_0_7), .in2(D__load), .in3(OutALU), .out(MUX_B_Out), .sel(MuxBSel));
  Part1_main main_3 (
    .FunSel(FunSel), .A0(MUX_C_Out[0]), .A1(MUX_C_Out[1]), .A2(MUX_C_Out[2]), .A3(MUX_C_Out[3]),
    .A4(MUX_C_Out[4]), .A5(MUX_C_Out[5]), .A6(MUX_C_Out[6]), .A7(MUX_C_Out[7]), .B0(OutB[0]), .B1(OutB[1]),
    .B2(OutB[2]), .B3(OutB[3]), .B4(OutB[4]), .B5(OutB[5]), .B6(OutB[6]), .B7(OutB[7]), .ZCNO(ZCNO),
    .OutALU0(OutALU[0]), .OutALU1(OutALU[1]), .OutALU2(OutALU[2]), .OutALU3(OutALU[3]), .OutALU4(OutALU[4]),
    .OutALU5(OutALU[5]), .OutALU6(OutALU[6]), .OutALU7(OutALU[7]));
  Part2b_final_main main_4 (
    .OutCSel(OutCSel), .OutDSel(OutDSel), .FunSel(FunSel_3), .RegSel(RegSel_2), .I0(MUX_B_Out[0]),
    .I1(MUX_B_Out[1]), .I2(MUX_B_Out[2]), .I3(MUX_B_Out[3]), .I4(MUX_B_Out[4]), .I5(MUX_B_Out[5]),
    .I6(MUX_B_Out[6]), .I7(MUX_B_Out[7]), .OutC0(OutC[0]), .OutD0(OutD[0]), .OutC1(OutC[1]), .OutD1(OutD[1]),
    .OutC2(OutC[2]), .OutB2(OutD[2]), .OutC3(OutC[3]), .OutD3(OutD[3]), .OutC4(OutC[4]), .OutD4(OutD[4]),
    .OutC5(OutC[5]), .OutD5(OutD[5]), .OutC6(OutC[6]), .OutD6(OutD[6]), .OutC7(OutC[7]), .OutD7(OutD[7]));
  Clock CLK (.out(CLK_out));
  RAM #(.bus("separate")) ram_1 (
    .addr(OutD), .din(OutALU), .data(D__load), .str(Str), .sel(Sel), .clk(CLK_out), .ld(LD), .clr(CLR));

  // Notes on the sheet:
  //   Register File
  //   MUX A
  //   IR
  //   MUX C
  //   MUX B
  //   ALU
  //   Address Register File
endmodule
