// Logisim project Part2a_final.circ as structural Verilog: 1 circuit, main circuit main
module main (
  input  [1:0] OutASel,
  input  [1:0] OutBSel,
  input  [1:0] FunSel,
  input  [3:0] RegSel,
  input  I0,
  input  I1,
  input  I2,
  input  I3,
  input  I4,
  input  I5,
  input  I6,
  input  I7,
  output OutA0,
  output OutB0,
  output OutA1,
  output OutB1,
  output OutA2,
  output OutB2,
  output OutA3,
  output OutB3,
  output OutA4,
  output OutB4,
  output OutA5,
  output OutB5,
  output OutA6,
  output OutB6,
  output OutA7,
  output OutB7
);

  wire R0_out_11, R0_out_12, R0_out_13, R0_out_14, R0_out_15, R0_out_16, R0_out_17, R0_out_18, R1_out_11,
       R1_out_12, R1_out_13, R1_out_14, R1_out_15, R1_out_16, R1_out_17, R1_out_18, R2_out_11, R2_out_12,
       R2_out_13, R2_out_14, R2_out_15, R2_out_16, R2_out_17, R2_out_18, R3_out_11, R3_out_12, R3_out_13,
       R3_out_14, R3_out_15, R3_out_16, R3_out_17, R3_out_18;

  Hex_Digit_Display hex_digit_display_1 (.value({I7, I6, I5, I4}));  // open: dp
  Hex_Digit_Display hex_digit_display_2 (.value({I3, I2, I1, I0}));  // open: dp
  _8bit_register_final_main R0 (
    .s1_s0(FunSel), .E(RegSel[0]), .out_11(R0_out_11), .I0(I0), .out_12(R0_out_12), .I1(I1),
    .out_13(R0_out_13), .I2(I2), .out_14(R0_out_14), .I3(I3), .out_15(R0_out_15), .I4(I4),
    .out_16(R0_out_16), .I5(I5), .out_17(R0_out_17), .I6(I6), .out_18(R0_out_18), .I7(I7));
  _8bit_register_final_main R1 (
    .s1_s0(FunSel), .E(RegSel[1]), .out_11(R1_out_11), .I0(I0), .out_12(R1_out_12), .I1(I1),
    .out_13(R1_out_13), .I2(I2), .out_14(R1_out_14), .I3(I3), .out_15(R1_out_15), .I4(I4),
    .out_16(R1_out_16), .I5(I5), .out_17(R1_out_17), .I6(I6), .out_18(R1_out_18), .I7(I7));
  _8bit_register_final_main R2 (
    .s1_s0(FunSel), .E(RegSel[2]), .out_11(R2_out_11), .I0(I0), .out_12(R2_out_12), .I1(I1),
    .out_13(R2_out_13), .I2(I2), .out_14(R2_out_14), .I3(I3), .out_15(R2_out_15), .I4(I4),
    .out_16(R2_out_16), .I5(I5), .out_17(R2_out_17), .I6(I6), .out_18(R2_out_18), .I7(I7));
  _8bit_register_final_main R3 (
    .s1_s0(FunSel), .E(RegSel[3]), .out_11(R3_out_11), .I0(I0), .out_12(R3_out_12), .I1(I1),
    .out_13(R3_out_13), .I2(I2), .out_14(R3_out_14), .I3(I3), .out_15(R3_out_15), .I4(I4),
    .out_16(R3_out_16), .I5(I5), .out_17(R3_out_17), .I6(I6), .out_18(R3_out_18), .I7(I7));
  Multiplexer #(.select(2)) multiplexer_1 (
    .in0(R0_out_11), .in1(R1_out_11), .in2(R2_out_11), .in3(R3_out_11), .out(OutA0), .sel(OutASel));  // open: en
  Multiplexer #(.select(2)) multiplexer_2 (
    .in0(R0_out_12), .in1(R1_out_12), .in2(R2_out_12), .in3(R3_out_12), .out(OutA1), .sel(OutASel));  // open: en
  Multiplexer #(.select(2)) multiplexer_3 (
    .in0(R0_out_13), .in1(R1_out_13), .in2(R2_out_13), .in3(R3_out_13), .out(OutA2), .sel(OutASel));  // open: en
  Multiplexer #(.select(2)) multiplexer_4 (
    .in0(R0_out_14), .in1(R1_out_14), .in2(R2_out_14), .in3(R3_out_14), .out(OutA3), .sel(OutASel));  // open: en
  Multiplexer #(.select(2)) multiplexer_5 (
    .in0(R0_out_15), .in1(R1_out_15), .in2(R2_out_15), .in3(R3_out_15), .out(OutA4), .sel(OutASel));  // open: en
  Multiplexer #(.select(2)) multiplexer_6 (
    .in0(R0_out_16), .in1(R1_out_16), .in2(R2_out_16), .in3(R3_out_16), .out(OutA5), .sel(OutASel));  // open: en
  Multiplexer #(.select(2)) multiplexer_7 (
    .in0(R0_out_17), .in1(R1_out_17), .in2(R2_out_17), .in3(R3_out_17), .out(OutA6), .sel(OutASel));  // open: en
  Multiplexer #(.select(2)) multiplexer_8 (
    .in0(R0_out_18), .in1(R1_out_18), .in2(R2_out_18), .in3(R3_out_18), .out(OutA7), .sel(OutASel));  // open: en
  Multiplexer #(.select(2)) multiplexer_9 (
    .in0(R0_out_11), .in1(R1_out_11), .in2(R2_out_11), .in3(R3_out_11), .out(OutB0), .sel(OutBSel));  // open: en
  Multiplexer #(.select(2)) multiplexer_10 (
    .in0(R0_out_12), .in1(R1_out_12), .in2(R2_out_12), .in3(R3_out_12), .out(OutB1), .sel(OutBSel));  // open: en
  Multiplexer #(.select(2)) multiplexer_11 (
    .in0(R0_out_13), .in1(R1_out_13), .in2(R2_out_13), .in3(R3_out_13), .out(OutB2), .sel(OutBSel));  // open: en
  Multiplexer #(.select(2)) multiplexer_12 (
    .in0(R0_out_14), .in1(R1_out_14), .in2(R2_out_14), .in3(R3_out_14), .out(OutB3), .sel(OutBSel));  // open: en
  Multiplexer #(.select(2)) multiplexer_13 (
    .in0(R0_out_15), .in1(R1_out_15), .in2(R2_out_15), .in3(R3_out_15), .out(OutB4), .sel(OutBSel));  // open: en
  Multiplexer #(.select(2)) multiplexer_14 (
    .in0(R0_out_16), .in1(R1_out_16), .in2(R2_out_16), .in3(R3_out_16), .out(OutB5), .sel(OutBSel));  // open: en
  Multiplexer #(.select(2)) multiplexer_15 (
    .in0(R0_out_17), .in1(R1_out_17), .in2(R2_out_17), .in3(R3_out_17), .out(OutB6), .sel(OutBSel));  // open: en
  Multiplexer #(.select(2)) multiplexer_16 (
    .in0(R0_out_18), .in1(R1_out_18), .in2(R2_out_18), .in3(R3_out_18), .out(OutB7), .sel(OutBSel));  // open: en
  Hex_Digit_Display hex_digit_display_3 (.value({OutA7, OutA6, OutA5, OutA4}));  // open: dp
  Hex_Digit_Display hex_digit_display_4 (.value({OutB7, OutB6, OutB5, OutB4}));  // open: dp
  Hex_Digit_Display hex_digit_display_5 (.value({OutA3, OutA2, OutA1, OutA0}));  // open: dp
  Hex_Digit_Display hex_digit_display_6 (.value({OutB3, OutB2, OutB1, OutB0}));  // open: dp

  // Notes on the sheet:
  //   OutA
  //   OutB
endmodule
