// Logisim project Part2b_final.circ as structural Verilog: 1 circuit, main circuit main
module main (
  input  [1:0] OutCSel,
  input  [1:0] OutDSel,
  input  [1:0] FunSel,
  input  [2:0] RegSel,
  input  I0,
  input  I1,
  input  I2,
  input  I3,
  input  I4,
  input  I5,
  input  I6,
  input  I7,
  output OutC0,
  output OutD0,
  output OutC1,
  output OutD1,
  output OutC2,
  output OutB2,
  output OutC3,
  output OutD3,
  output OutC4,
  output OutD4,
  output OutC5,
  output OutD5,
  output OutC6,
  output OutD6,
  output OutC7,
  output OutD7
);

  wire AR_out_11, AR_out_12, AR_out_13, AR_out_14, AR_out_15, AR_out_16, AR_out_17, AR_out_18, PC_out_11,
       PC_out_12, PC_out_13, PC_out_14, PC_out_15, PC_out_16, PC_out_17, PC_out_18, SP_out_11, SP_out_12,
       SP_out_13, SP_out_14, SP_out_15, SP_out_16, SP_out_17, SP_out_18;

  Hex_Digit_Display hex_digit_display_1 (.value({I7, I6, I5, I4}));  // open: dp
  Hex_Digit_Display hex_digit_display_2 (.value({{2{I2}}, I1, I0}));  // open: dp
  _8bit_register_final_main PC (
    .s1_s0(FunSel), .E(RegSel[0]), .out_11(PC_out_11), .I0(I0), .out_12(PC_out_12), .I1(I1),
    .out_13(PC_out_13), .I2(I2), .out_14(PC_out_14), .I3(I3), .out_15(PC_out_15), .I4(I4),
    .out_16(PC_out_16), .I5(I5), .out_17(PC_out_17), .I6(I6), .out_18(PC_out_18), .I7(I7));
  _8bit_register_final_main AR (
    .s1_s0(FunSel), .E(RegSel[1]), .out_11(AR_out_11), .I0(I0), .out_12(AR_out_12), .I1(I1),
    .out_13(AR_out_13), .I2(I2), .out_14(AR_out_14), .I3(I3), .out_15(AR_out_15), .I4(I4),
    .out_16(AR_out_16), .I5(I5), .out_17(AR_out_17), .I6(I6), .out_18(AR_out_18), .I7(I7));
  _8bit_register_final_main SP (
    .s1_s0(FunSel), .E(RegSel[2]), .out_11(SP_out_11), .I0(I0), .out_12(SP_out_12), .I1(I1),
    .out_13(SP_out_13), .I2(I2), .out_14(SP_out_14), .I3(I3), .out_15(SP_out_15), .I4(I4),
    .out_16(SP_out_16), .I5(I5), .out_17(SP_out_17), .I6(I6), .out_18(SP_out_18), .I7(I7));
  Multiplexer #(.select(2)) multiplexer_1 (
    .in0(PC_out_11), .in1(AR_out_11), .in2(SP_out_11), .in3(PC_out_11), .out(OutC0), .sel(OutCSel));  // open: en
  Multiplexer #(.select(2)) multiplexer_2 (
    .in0(PC_out_12), .in1(AR_out_12), .in2(SP_out_12), .in3(PC_out_12), .out(OutC1), .sel(OutCSel));  // open: en
  Multiplexer #(.select(2)) multiplexer_3 (
    .in0(PC_out_13), .in1(AR_out_13), .in2(SP_out_13), .in3(PC_out_13), .out(OutC2), .sel(OutCSel));  // open: en
  Multiplexer #(.select(2)) multiplexer_4 (
    .in0(PC_out_14), .in1(AR_out_14), .in2(SP_out_14), .in3(PC_out_14), .out(OutC3), .sel(OutCSel));  // open: en
  Multiplexer #(.select(2)) multiplexer_5 (
    .in0(PC_out_15), .in1(AR_out_15), .in2(SP_out_15), .in3(PC_out_15), .out(OutC4), .sel(OutCSel));  // open: en
  Multiplexer #(.select(2)) multiplexer_6 (
    .in0(PC_out_16), .in1(AR_out_16), .in2(SP_out_16), .in3(PC_out_16), .out(OutC5), .sel(OutCSel));  // open: en
  Multiplexer #(.select(2)) multiplexer_7 (
    .in0(PC_out_17), .in1(AR_out_17), .in2(SP_out_17), .in3(PC_out_17), .out(OutC6), .sel(OutCSel));  // open: en
  Multiplexer #(.select(2)) multiplexer_8 (
    .in0(PC_out_18), .in1(AR_out_18), .in2(SP_out_18), .in3(PC_out_18), .out(OutC7), .sel(OutCSel));  // open: en
  Multiplexer #(.select(2)) multiplexer_9 (
    .in0(PC_out_11), .in1(AR_out_11), .in2(SP_out_11), .in3(PC_out_11), .out(OutD0), .sel(OutDSel));  // open: en
  Multiplexer #(.select(2)) multiplexer_10 (
    .in0(PC_out_12), .in1(AR_out_12), .in2(SP_out_12), .in3(PC_out_12), .out(OutD1), .sel(OutDSel));  // open: en
  Multiplexer #(.select(2)) multiplexer_11 (
    .in0(PC_out_13), .in1(AR_out_13), .in2(SP_out_13), .in3(PC_out_13), .out(OutB2), .sel(OutDSel));  // open: en
  Multiplexer #(.select(2)) multiplexer_12 (
    .in0(PC_out_14), .in1(AR_out_14), .in2(SP_out_14), .in3(PC_out_14), .out(OutD3), .sel(OutDSel));  // open: en
  Multiplexer #(.select(2)) multiplexer_13 (
    .in0(PC_out_15), .in1(AR_out_15), .in2(SP_out_15), .in3(PC_out_15), .out(OutD4), .sel(OutDSel));  // open: en
  Multiplexer #(.select(2)) multiplexer_14 (
    .in0(PC_out_16), .in1(AR_out_16), .in2(SP_out_16), .in3(PC_out_16), .out(OutD5), .sel(OutDSel));  // open: en
  Multiplexer #(.select(2)) multiplexer_15 (
    .in0(PC_out_17), .in1(AR_out_17), .in2(SP_out_17), .in3(PC_out_17), .out(OutD6), .sel(OutDSel));  // open: en
  Multiplexer #(.select(2)) multiplexer_16 (
    .in0(PC_out_18), .in1(AR_out_18), .in2(SP_out_18), .in3(PC_out_18), .out(OutD7), .sel(OutDSel));  // open: en
  Hex_Digit_Display hex_digit_display_3 (.value({OutC7, OutC6, OutC5, OutC4}));  // open: dp
  Hex_Digit_Display hex_digit_display_4 (.value({OutD7, OutD6, OutD5, OutD4}));  // open: dp
  Hex_Digit_Display hex_digit_display_5 (.value({OutC3, OutC2, OutC1, OutC0}));  // open: dp
  Hex_Digit_Display hex_digit_display_6 (.value({OutD3, OutB2, OutD1, OutD0}));  // open: dp

  // Notes on the sheet:
  //   OutC
  //   OutD
endmodule
