// Logisim project Part2c_final_FunSel.circ as structural Verilog: 1 circuit, main circuit main
module main (
  input  [1:0] FunSel,
  input  L_prime_H,
  input  E,
  input  I0,
  input  I1,
  input  I2,
  input  I3,
  input  I4,
  input  I5,
  input  I6,
  input  I7,
  output O0,
  output O1,
  output O2,
  output O3,
  output O4,
  output O5,
  output O6,
  output O7,
  output O8,
  output O9,
  output O10,
  output O11,
  output O12,
  output O13,
  output O14,
  output O15
);

  wire controlled_buffer_1_out, controlled_buffer_2_out, controlled_buffer_3_out, controlled_buffer_4_out,
       controlled_buffer_5_out, controlled_buffer_6_out, controlled_buffer_7_out, controlled_buffer_8_out,
       controlled_buffer_9_out, controlled_buffer_10_out, controlled_buffer_11_out, controlled_buffer_12_out,
       controlled_buffer_13_out, controlled_buffer_14_out, controlled_buffer_15_out,
       controlled_buffer_16_out, not_1_out;
  wire [1:1] xor_1_out;

  Hex_Digit_Display hex_digit_display_1 (.value({I7, I6, I5, I4}));  // open: dp
  Hex_Digit_Display hex_digit_display_2 (.value({I3, I2, I1, I0}));  // open: dp
  not not_1 (not_1_out, L_prime_H);
  assign controlled_buffer_1_out = not_1_out ? I0 : 1'bz;  // Controlled_Buffer controlled_buffer_1
  assign controlled_buffer_2_out = not_1_out ? I1 : 1'bz;  // Controlled_Buffer controlled_buffer_2
  assign controlled_buffer_3_out = not_1_out ? I2 : 1'bz;  // Controlled_Buffer controlled_buffer_3
  assign controlled_buffer_4_out = not_1_out ? I3 : 1'bz;  // Controlled_Buffer controlled_buffer_4
  assign controlled_buffer_5_out = not_1_out ? I4 : 1'bz;  // Controlled_Buffer controlled_buffer_5
  assign controlled_buffer_6_out = not_1_out ? I5 : 1'bz;  // Controlled_Buffer controlled_buffer_6
  assign controlled_buffer_7_out = not_1_out ? I6 : 1'bz;  // Controlled_Buffer controlled_buffer_7
  assign controlled_buffer_8_out = not_1_out ? I7 : 1'bz;  // Controlled_Buffer controlled_buffer_8
  assign controlled_buffer_9_out = L_prime_H ? I0 : 1'bz;  // Controlled_Buffer controlled_buffer_9
  assign controlled_buffer_10_out = L_prime_H ? I1 : 1'bz;  // Controlled_Buffer controlled_buffer_10
  assign controlled_buffer_11_out = L_prime_H ? I2 : 1'bz;  // Controlled_Buffer controlled_buffer_11
  assign controlled_buffer_12_out = L_prime_H ? I3 : 1'bz;  // Controlled_Buffer controlled_buffer_12
  assign controlled_buffer_13_out = L_prime_H ? I4 : 1'bz;  // Controlled_Buffer controlled_buffer_13
  assign controlled_buffer_14_out = L_prime_H ? I5 : 1'bz;  // Controlled_Buffer controlled_buffer_14
  assign controlled_buffer_15_out = L_prime_H ? I6 : 1'bz;  // Controlled_Buffer controlled_buffer_15
  assign controlled_buffer_16_out = L_prime_H ? I7 : 1'bz;  // Controlled_Buffer controlled_buffer_16
  xor xor_1 (xor_1_out[1], FunSel[1], FunSel[0]);
  _16bit_register_final_main IR (
    .s1_s0({xor_1_out[1], FunSel[1]}), .E(E), .I0(controlled_buffer_1_out), .I1(controlled_buffer_2_out),
    .I2(controlled_buffer_3_out), .I3(controlled_buffer_4_out), .I4(controlled_buffer_5_out),
    .I5(controlled_buffer_6_out), .I6(controlled_buffer_7_out), .I7(controlled_buffer_8_out),
    .I8(controlled_buffer_9_out), .I9(controlled_buffer_10_out), .I10(controlled_buffer_11_out),
    .I11(controlled_buffer_12_out), .I12(controlled_buffer_13_out), .I13(controlled_buffer_14_out),
    .I14(controlled_buffer_15_out), .I15(controlled_buffer_16_out), .out_19(O0), .out_20(O1), .out_21(O2),
    .out_22(O3), .out_23(O4), .out_24(O5), .out_25(O6), .out_26(O7), .out_27(O8), .out_28(O9), .out_29(O10),
    .out_30(O11), .out_31(O12), .out_32(O13), .out_33(O14), .out_34(O15));
  Hex_Digit_Display hex_digit_display_3 (.value({O15, O14, O13, O12}));  // open: dp
  Hex_Digit_Display hex_digit_display_4 (.value({O11, O10, O9, O8}));  // open: dp
  Hex_Digit_Display hex_digit_display_5 (.value({O7, O6, O5, O4}));  // open: dp
  Hex_Digit_Display hex_digit_display_6 (.value({O3, O2, O1, O0}));  // open: dp
endmodule
