// Logisim project Shifting_Unit.circ as structural Verilog: 1 circuit, main circuit main
module main (
  input  s2,
  input  s1,
  input  s0,
  input  CARRY_IN,
  input  A0,
  input  A1,
  input  A2,
  input  A3,
  input  A4,
  input  A5,
  input  A6,
  input  A7,
  output O0,
  output O1,
  output O2,
  output O3,
  output O4,
  output O5,
  output O6,
  output O7,
  output CARRY_OUT
);

  wire and_1_out, multiplexer_1_out, multiplexer_2_out, multiplexer_3_out, or_1_out;

  and and_1 (and_1_out, s2, s1);
  or or_1 (or_1_out, and_1_out, s0);
  Multiplexer #(.enable("false")) multiplexer_1 (.in0(A7), .in1(CARRY_IN), .out(multiplexer_1_out), .sel(s1));
  Multiplexer #(.enable("false")) multiplexer_2 (.in0(1'b0), .in1(CARRY_IN), .out(multiplexer_2_out), .sel(or_1_out));
  Multiplexer #(.enable("false")) multiplexer_3 (
    .in0(1'b0), .in1(multiplexer_1_out), .out(multiplexer_3_out), .sel(s2));
  Multiplexer #(.enable("false")) multiplexer_4 (.in0(multiplexer_2_out), .in1(A1), .out(O0), .sel(s0));
  Multiplexer #(.enable("false")) multiplexer_5 (.in0(A0), .in1(A2), .out(O1), .sel(s0));
  Multiplexer #(.enable("false")) multiplexer_6 (.in0(A1), .in1(A3), .out(O2), .sel(s0));
  Multiplexer #(.enable("false")) multiplexer_7 (.in0(A2), .in1(A4), .out(O3), .sel(s0));
  Multiplexer #(.enable("false")) multiplexer_8 (.in0(A3), .in1(A5), .out(O4), .sel(s0));
  Multiplexer #(.enable("false")) multiplexer_9 (.in0(A4), .in1(A6), .out(O5), .sel(s0));
  Multiplexer #(.enable("false")) multiplexer_10 (.in0(A5), .in1(A7), .out(O6), .sel(s0));
  Multiplexer #(.enable("false")) multiplexer_11 (.in0(A6), .in1(multiplexer_3_out), .out(O7), .sel(s0));
  Multiplexer #(.enable("false")) multiplexer_12 (.in0(A7), .in1(A0), .out(CARRY_OUT), .sel(s0));
endmodule
