// Logisim project ZCNO_Register.circ as structural Verilog: 1 circuit, main circuit main
module main (
  input  [3:0] FunSel,
  input  OutALU0,
  input  OutALU1,
  input  OutALU2,
  input  OutALU3,
  input  OutALU4,
  input  OutALU5,
  input  OutALU6,
  input  OutALU7,
  input  C_arithmetic,
  input  C_shifting,
  input  A6,
  input  A7,
  input  B7,
  output ZERO,
  output CARRY,
  output NEGATIVE,
  output OVERFLOW
);

  wire and_1_out, and_2_out, clock_1_out, multiplexer_1_out, multiplexer_2_out, multiplexer_3_out,
       multiplexer_4_out, multiplexer_5_out, nor_1_out, xnor_1_out, xnor_2_out, xor_1_out, xor_2_out,
       xor_3_out, xor_4_out;

  xnor xnor_1 (xnor_1_out, A7, B7);
  xor xor_1 (xor_1_out, A7, OutALU7);
  xor xor_2 (xor_2_out, A7, B7);
  xnor xnor_2 (xnor_2_out, B7, OutALU7);
  xor xor_3 (xor_3_out, A6, A7);
  xor xor_4 (xor_4_out, CARRY, A7);
  and and_1 (and_1_out, xnor_1_out, xor_1_out);
  and and_2 (and_2_out, xor_2_out, xnor_2_out);
  Clock clock_1 (.out(clock_1_out));
  nor nor_1 (nor_1_out, OutALU0, OutALU1, OutALU2, OutALU3, OutALU4, OutALU5, OutALU6, OutALU7);
  Multiplexer #(.select(4), .enable("false")) multiplexer_1 (
    .in0(1'b0), .in1(1'b0), .in2(1'b0), .in3(1'b0), .in4(C_arithmetic), .in5(C_arithmetic),
    .in6(C_arithmetic), .in7(1'b0), .in8(1'b0), .in9(1'b0), .in10(C_shifting), .in11(C_shifting),
    .in12(1'b0), .in13(1'b0), .in14(C_shifting), .in15(C_shifting), .out(multiplexer_1_out), .sel(FunSel));
  Multiplexer #(.select(4), .enable("false")) multiplexer_2 (
    .in0(1'b0), .in1(1'b0), .in2(1'b0), .in3(1'b0), .in4(1'b1), .in5(1'b1), .in6(1'b1), .in7(1'b0),
    .in8(1'b0), .in9(1'b0), .in10(1'b1), .in11(1'b1), .in12(1'b0), .in13(1'b0), .in14(1'b1), .in15(1'b1),
    .out(multiplexer_2_out), .sel(FunSel));
  Multiplexer #(.select(4), .enable("false")) multiplexer_3 (
    .in0(1'b1), .in1(1'b1), .in2(1'b1), .in3(1'b1), .in4(1'b1), .in5(1'b1), .in6(1'b1), .in7(1'b1),
    .in8(1'b1), .in9(1'b1), .in10(1'b1), .in11(1'b1), .in12(1'b1), .in13(1'b0), .in14(1'b1), .in15(1'b1),
    .out(multiplexer_3_out), .sel(FunSel));
  Multiplexer #(.select(4), .enable("false")) multiplexer_4 (
    .in0(1'b0), .in1(1'b0), .in2(1'b0), .in3(1'b0), .in4(and_1_out), .in5(and_1_out), .in6(and_2_out),
    .in7(1'b0), .in8(1'b0), .in9(1'b0), .in10(1'b0), .in11(1'b0), .in12(xor_3_out), .in13(1'b0),
    .in14(xor_3_out), .in15(xor_4_out), .out(multiplexer_4_out), .sel(FunSel));
  Multiplexer #(.select(4), .enable("false")) multiplexer_5 (
    .in0(1'b0), .in1(1'b0), .in2(1'b0), .in3(1'b0), .in4(1'b1), .in5(1'b1), .in6(1'b1), .in7(1'b0),
    .in8(1'b0), .in9(1'b0), .in10(1'b0), .in11(1'b0), .in12(1'b1), .in13(1'b0), .in14(1'b1), .in15(1'b1),
    .out(multiplexer_5_out), .sel(FunSel));
  D_Flip_Flop u_ZERO (.clk(clock_1_out), .D(nor_1_out), .Q(ZERO), .en(1'b1));  // open: Qn, preset, reset
  D_Flip_Flop u_CARRY (
    .clk(clock_1_out), .D(multiplexer_1_out), .Q(CARRY), .en(multiplexer_2_out));  // open: Qn, preset, reset
  D_Flip_Flop u_NEGATIVE (
    .clk(clock_1_out), .D(OutALU7), .Q(NEGATIVE), .en(multiplexer_3_out));  // open: Qn, preset, reset
  D_Flip_Flop u_OVERFLOW (
    .clk(clock_1_out), .D(multiplexer_4_out), .Q(OVERFLOW), .en(multiplexer_5_out));  // open: Qn, preset, reset
endmodule
